# Fritzing sketch Arduponiav2Circuito (saved by Fritzing 0.8.7b)
breadboards: 1

parts:
  Part1 = Arduino Due (Rev2b)
  U1 = G3VM-61E1 [package=g3vm-61e1]
  M1 = DC Motor
  RHT1 = Humidity and Temperature Sensor RHT03
  U3 = HIH-4030 [package=hih-4030]
  Part2 = Triple Axis Accelerometer Breakout - ADXL345

nets:
  N1: Part1.A0, U3.OUT
  N2: Part1.D20/SDA3, Part2.SDA
  N3: Part1.D21/SCL3, Part2.SCL
  N4: Part1.IOREF, Part2.VCC
  N5: Part1.5V, U1.P$2, U1.P$5
  GND: Part1.GND, U1.P$4, M1.pin_1, RHT1.GND_2, U3.GND, Part2.GND
  N6: Part1.D8_PWM, U3.VCC
  N7: Part1.D9_PWM, RHT1.Data-signal
  N8: Part1.D10_PWM/SS0, RHT1.GND_1
  N9: Part1.D36, U1.P$6
  N10: U1.P$1, M1.pin_2
